// Logisim project SUMA.circ as structural Verilog: 3 circuits, main circuit main
module main (
  input  in_1,
  input  in_2,
  input  in_3,
  input  in_4,
  input  in_5,
  input  in_6,
  input  in_7,
  input  in_8,
  output out_9,
  output out_10,
  output out_11,
  output out_12
);

  wire semisuma1_1_acarreo, sumacompleta_1_acarreo, sumacompleta_2_acarreo;

  SemiSuma1 semisuma1_1 (.A(in_4), .B(in_8), .SUMA(out_12), .ACARREO(semisuma1_1_acarreo));
  SUMACOMPLETA sumacompleta_1 (
    .A(in_3), .B(in_7), .Cin(semisuma1_1_acarreo), .SUMA(out_11), .ACARREO(sumacompleta_1_acarreo));
  SUMACOMPLETA sumacompleta_2 (
    .A(in_2), .B(in_6), .Cin(sumacompleta_1_acarreo), .SUMA(out_10), .ACARREO(sumacompleta_2_acarreo));
  SUMACOMPLETA sumacompleta_3 (.A(in_1), .B(in_5), .Cin(sumacompleta_2_acarreo), .SUMA(out_9));  // open: ACARREO
endmodule

module SemiSuma1 (
  input  A,
  input  B,
  output SUMA,
  output ACARREO
);

  xor xor_1 (SUMA, A, B);
  and and_1 (ACARREO, A, B);
endmodule

module SUMACOMPLETA (
  input  A,
  input  B,
  input  Cin,
  output SUMA,
  output ACARREO
);

  wire and_1_out, and_2_out, xor_1_out;

  xor xor_1 (xor_1_out, A, B);
  and and_1 (and_1_out, xor_1_out, Cin);
  and and_2 (and_2_out, A, B);
  or or_1 (ACARREO, and_1_out, and_2_out);
  xor xor_2 (SUMA, xor_1_out, Cin);
endmodule
